# Fritzing sketch Schema_elettrico_cravatte (saved by Fritzing 0.8.5b)
breadboards: 1

parts:
  ARDUINO_LILYPAD = Lilypad Arduino Board
  LED_ROSSO_3 = LilyPad LED
  MICROFONO = Breakout Board for Electret Microphone
  LED_VERDE_1 = LilyPad LED
  LED_VERDE_2 = LilyPad LED
  LED_VERDE_3 = LilyPad LED
  LED_ARANCIONE_1 = LilyPad LED
  LED_ARANCIONE_2 = LilyPad LED
  LED_ARANCIONE_3 = LilyPad LED
  LED_ROSSO_1 = LilyPad LED
  LED_ROSSO_2 = LilyPad LED
  PULSANTE = LilyPad Button Board

nets (from the schematic view):
  GND: ARDUINO_LILYPAD.GND, LED_ROSSO_3.-, MICROFONO.GND, LED_VERDE_1.-, LED_VERDE_2.-, LED_VERDE_3.-, LED_ARANCIONE_1.-, LED_ARANCIONE_2.-, LED_ARANCIONE_3.-, LED_ROSSO_1.-, LED_ROSSO_2.-
  N1: ARDUINO_LILYPAD.A0, MICROFONO.AUD
  N2: ARDUINO_LILYPAD.D8, LED_ARANCIONE_3.+
  N3: ARDUINO_LILYPAD.D9, LED_ROSSO_1.+
  N4: ARDUINO_LILYPAD.D10, LED_ROSSO_2.+
  N5: ARDUINO_LILYPAD.MISO/D12, PULSANTE.-
  N6: ARDUINO_LILYPAD.SCK/D13, LED_ROSSO_3.+
  N7: ARDUINO_LILYPAD.D6, LED_ARANCIONE_1.+
  N8: ARDUINO_LILYPAD.D5, LED_VERDE_3.+
  N9: ARDUINO_LILYPAD.D4, LED_VERDE_2.+
  N10: ARDUINO_LILYPAD.D3, LED_VERDE_1.+
  N11: ARDUINO_LILYPAD.D7, LED_ARANCIONE_2.+
  VCC: ARDUINO_LILYPAD.VCC, MICROFONO.VCC, PULSANTE.S
